# Fritzing sketch Wespi-P1Jupiter (saved by Fritzing 0.9.4)
breadboards: 1

parts:
  R1 = Resistor [tolerance=±5% resistance=390 package=THT]
  R2 = Resistor [tolerance=±5% resistance=390 package=THT]
  R3 = Resistor [tolerance=±5% resistance=390 package=THT]
  R4 = Resistor [tolerance=±5% resistance=390 package=THT]
  C1 = Ceramic Capacitor [capacitance=47nF package="100 mil [THT, multilayer]"]
  C2 = Ceramic Capacitor [capacitance=47nF package="100 mil [THT, multilayer]"]
  SPK1 = Piezo Speaker
  R5 = Resistor [tolerance=±5% resistance=10k package=THT]

nets:
  N1: R1.Pin_0, C1.1
  Tape OUT: R1.Pin_1
  N2: R2.Pin_0, C2.1
  Tape IN: R2.Pin_1
  N3: R3.Pin_0, SPK1.pin2
  Speaker: R3.Pin_1
  Wespi GND: R4.Pin_0, SPK1.pin1, R5.Pin_1
  GND: R4.Pin_1
  Wespi TAP_INP D25: C1.0
  Wespi TAP_OUT D22: C2.0, R5.Pin_0
